# Fritzing sketch Taller2 esquematico (saved by Fritzing 0.9.3b)
circuit board: 8.46667cm x 5.95802cm

parts:
  U1 = ESP8266 WiFi Module [part_number=ESP8266]
  Componente1 = Arduino Uno (Rev3)
  Componente2 = RFID-RC522-v2

nets:
  N1: U1.RXD, Componente1.D0/RX
  VCC: U1.VCC, U1.CH_PD, Componente1.3V3, Componente2.3.3V
  GND: U1.GND, Componente1.GND, Componente2.GND
  N2: U1.TXD, Componente1.D1/TX
  N3: Componente1.D9_PWM, Componente2.RST
  N4: Componente1.D10_PWM/SS, Componente2.SDA
  N5: Componente1.D11_PWM/MOSI, Componente2.MOSI
  N6: Componente1.D12/MISO, Componente2.MISO
  N7: Componente1.D13/SCK, Componente2.SCK

custom parts:
  ESP8266 WiFi Module: Generic WiFi Module based on the ESP8266 with onboard PCB antenna and UART communications
  RFID-RC522-v2: A simple China made RFID-RC522 Reader; do check the pin labels, as this is a MFRC522 based clone.
