# Fritzing sketch Taller2 proto (saved by Fritzing 0.9.3b)

parts:
  U1 = ESP8266 WiFi Module [part_number=ESP8266]
  Componente2 = RFID-RC522-v2
  Componente3 = Arduino Uno (Rev3)

nets:
  N1: U1.RXD, Componente3.D0/RX
  VCC: U1.VCC, U1.CH_PD, Componente2.3.3V, Componente3.3V3
  GND: U1.GND, Componente2.GND, Componente3.GND
  N2: U1.TXD, Componente3.D1/TX
  N3: Componente2.SDA, Componente3.D10_PWM/SS
  N4: Componente2.SCK, Componente3.D13/SCK
  N5: Componente2.MOSI, Componente3.D11_PWM/MOSI
  N6: Componente2.MISO, Componente3.D12/MISO
  N7: Componente2.RST, Componente3.D9_PWM

custom parts:
  ESP8266 WiFi Module: Generic WiFi Module based on the ESP8266 with onboard PCB antenna and UART communications
  RFID-RC522-v2: A simple China made RFID-RC522 Reader; do check the pin labels, as this is a MFRC522 based clone.
